// Logisim project Compu.circ as structural Verilog
module main (
  input  [9:0] RELOAD,
  input  [59:0] in_2,
  input  CACHE_IN_READ,
  input  [39:0] in_4,
  output [7:0] out_5,
  output [7:0] out_6
);

  wire and_2_out, and_3_out, and_4_out, BufferInScreen_q, clock_1_out, comparator_3_eq, comparator_3_lt,
       comparator_4_eq, d_ff_1_q, d_ff_2_q, demultiplexer_1_out1, demultiplexer_1_out2, demultiplexer_1_out3,
       demultiplexer_1_out4, demultiplexer_1_out5, demultiplexer_1_out6, demultiplexer_1_out7,
       demultiplexer_1_out8, demultiplexer_1_out9, demultiplexer_1_out10, not_1_out, not_3_out, not_4_out,
       not_5_out, or_2_out, or_3_out, ram_load_read_controller_1_load, ram_load_read_controller_1_store,
       ram_load_read_controller_2_load, ram_load_read_controller_2_store, ram_load_read_controller_3_load,
       ram_load_read_controller_3_store, ram_load_read_controller_4_load, ram_load_read_controller_4_store,
       ram_load_read_controller_5_load, ram_load_read_controller_5_store, RESET_out, s_r_ff_1_q;
  wire [2:0] comparator_1_gt, comparator_2_gt, IR_q_2, multiplier_3_cout, multiplier_3_out;
  wire [5:0] bit_extender_9_out, counter_1_q, divider_3_out, divider_3_rem;
  wire [7:0] IR_q;
  wire [9:0] multiplexer_1_out, multiplexer_2_out, multiplexer_3_out, multiplexer_5_out, PC_q;
  wire [13:0] ADR_CACHE_q, multiplexer_7_out;
  wire [15:0] adder_3_out, multiplexer_10_out, multiplexer_11_out, SCREEN_q;
  wire [23:0] adder_1_out, adder_2_out, and_1_out, bit_extender_5_out, bit_extender_6_out,
       bit_extender_10_out, demultiplexer_2_out0, demultiplexer_2_out1, divider_1_out, divider_1_rem,
       divider_2_out, divider_2_rem, FrameBuffer0_dout, FrameBuffer1_dout, multiplexer_6_out,
       multiplier_1_cout, multiplier_1_out, multiplier_2_cout, multiplier_2_out, not_2_out, or_1_out,
       Resources_data, rgb_video_1_p6, subtractor_1_out, xor_1_out;
  wire [39:0] ram_2_dout, ram_4_dout;
  wire [39:10] PC_q_2;
  wire [47:0] bit_extender_1_out, bit_extender_2_out, bit_extender_3_out, bit_extender_4_out, GPU_INST_q,
       multiplexer_4_out;
  wire [47:14] multiplexer_7_out_2;
  wire [51:0] bit_extender_7_out, bit_extender_8_out, CACHE_L2_dout, COMPLEX_ALU_DATA_q, IR_q_3, R0_q, R1_q,
       R2_q, R3_q, SIMPLE_ALU_DATA_q;
  wire [51:48] multiplexer_7_out_3;
  wire [59:0] multiplexer_8_out, ram_1_dout, ram_3_dout;

  Register #(.width(52)) SIMPLE_ALU_DATA (
    .D({multiplexer_7_out_3, multiplexer_7_out_2, multiplexer_7_out}), .en(demultiplexer_1_out1),
    .clk(clock_1_out), .Q(SIMPLE_ALU_DATA_q), .clr(and_2_out));
  Register #(.width(52)) COMPLEX_ALU_DATA (
    .D({multiplexer_7_out_3, multiplexer_7_out_2, multiplexer_7_out}), .en(demultiplexer_1_out2),
    .clk(clock_1_out), .Q(COMPLEX_ALU_DATA_q), .clr(and_2_out));
  Clock clock_1 (.out(clock_1_out));
  Button RESET (.out(RESET_out));
  D_Flip_Flop d_ff_1 (.D(RESET_out), .clk(clock_1_out), .Q(d_ff_1_q));  // open: Qn, preset, reset
  not not_1 (not_1_out, d_ff_1_q);
  Adder #(.width(24)) adder_1 (
    .a(SIMPLE_ALU_DATA_q[23:0]), .b(SIMPLE_ALU_DATA_q[47:24]), .out(adder_1_out));  // open: cin, cout
  Subtractor #(.width(24)) subtractor_1 (
    .a(SIMPLE_ALU_DATA_q[23:0]), .b(SIMPLE_ALU_DATA_q[47:24]), .out(subtractor_1_out));  // open: bin, bout
  assign and_1_out = SIMPLE_ALU_DATA_q[23:0] & SIMPLE_ALU_DATA_q[47:24];  // AND_Gate and_1, 24 bits wide
  assign or_1_out = SIMPLE_ALU_DATA_q[23:0] | SIMPLE_ALU_DATA_q[47:24];  // OR_Gate or_1, 24 bits wide
  assign xor_1_out = SIMPLE_ALU_DATA_q[23:0] ^ SIMPLE_ALU_DATA_q[47:24];  // XOR_Gate xor_1, 24 bits wide
  assign not_2_out = ~SIMPLE_ALU_DATA_q[23:0];  // NOT_Gate not_2, 24 bits wide
  Comparator #(.mode("unsigned"), .width(24)) comparator_1 (
    .a(SIMPLE_ALU_DATA_q[23:0]), .b(SIMPLE_ALU_DATA_q[47:24]), .gt(comparator_1_gt[0]),
    .eq(comparator_1_gt[1]), .lt(comparator_1_gt[2]));
  Comparator #(.width(24)) comparator_2 (
    .a(SIMPLE_ALU_DATA_q[23:0]), .b(SIMPLE_ALU_DATA_q[47:24]), .gt(comparator_2_gt[0]),
    .eq(comparator_2_gt[1]), .lt(comparator_2_gt[2]));
  Multiplier #(.width(24)) multiplier_1 (
    .a(COMPLEX_ALU_DATA_q[23:0]), .b(COMPLEX_ALU_DATA_q[47:24]), .out(multiplier_1_out),
    .cout(multiplier_1_cout));  // open: cin
  Multiplier #(.mode("twosComplement"), .width(24)) multiplier_2 (
    .a(COMPLEX_ALU_DATA_q[23:0]), .b(COMPLEX_ALU_DATA_q[47:24]), .out(multiplier_2_out),
    .cout(multiplier_2_cout));  // open: cin
  assign bit_extender_1_out = {{24{1'b0}}, divider_1_out};  // Bit_Extender bit_extender_1
  Divider #(.width(24)) divider_1 (
    .a(COMPLEX_ALU_DATA_q[23:0]), .b(COMPLEX_ALU_DATA_q[47:24]), .out(divider_1_out), .rem(divider_1_rem));  // open: upper
  assign bit_extender_2_out = {{24{1'b0}}, divider_1_rem};  // Bit_Extender bit_extender_2
  assign bit_extender_3_out = {{24{1'b0}}, divider_2_out};  // Bit_Extender bit_extender_3
  Divider #(.mode("twosComplement"), .width(24)) divider_2 (
    .a(COMPLEX_ALU_DATA_q[23:0]), .b(COMPLEX_ALU_DATA_q[47:24]), .out(divider_2_out), .rem(divider_2_rem));  // open: upper
  assign bit_extender_4_out = {{24{1'b0}}, divider_2_rem};  // Bit_Extender bit_extender_4
  and and_2 (and_2_out, RESET_out, not_1_out);
  Multiplexer #(.width(10)) multiplexer_1 (.in0(PC_q), .in1(RELOAD), .out(multiplexer_1_out), .sel(CACHE_IN_READ));
  RAM_LOAD_READ_CONTROLLER ram_load_read_controller_1 (
    .STORE_SIGNAL(CACHE_IN_READ), .LOAD(ram_load_read_controller_1_load),
    .STORE(ram_load_read_controller_1_store));
  Multiplexer #(.width(10)) multiplexer_2 (.in0(PC_q), .in1(RELOAD), .out(multiplexer_2_out), .sel(CACHE_IN_READ));
  RAM_LOAD_READ_CONTROLLER ram_load_read_controller_2 (
    .STORE_SIGNAL(not_3_out), .LOAD(ram_load_read_controller_2_load), .STORE(ram_load_read_controller_2_store));
  not not_3 (not_3_out, CACHE_IN_READ);
  Multiplexer #(.width(10)) multiplexer_3 (.in0(PC_q), .in1(RELOAD), .out(multiplexer_3_out), .sel(not_3_out));
  assign bit_extender_5_out = {{21{1'b0}}, comparator_1_gt};  // Bit_Extender bit_extender_5
  assign bit_extender_6_out = {{21{1'b0}}, comparator_2_gt};  // Bit_Extender bit_extender_6
  Multiplexer #(.select(3), .width(48)) multiplexer_4 (
    .in0({multiplier_1_cout, multiplier_1_out}), .in1({multiplier_2_cout, multiplier_2_out}),
    .in2(bit_extender_1_out), .in3(bit_extender_2_out), .in4(bit_extender_3_out), .in5(bit_extender_4_out),
    .out(multiplexer_4_out), .sel(COMPLEX_ALU_DATA_q[51:49]));  // open: in6, in7
  Demultiplexer #(.select(4)) demultiplexer_1 (
    .out1(demultiplexer_1_out1), .out2(demultiplexer_1_out2), .out3(demultiplexer_1_out3),
    .out4(demultiplexer_1_out4), .out5(demultiplexer_1_out5), .out6(demultiplexer_1_out6),
    .out7(demultiplexer_1_out7), .out8(demultiplexer_1_out8), .out9(demultiplexer_1_out9),
    .out10(demultiplexer_1_out10), .in(1'b1), .sel(IR_q[3:0]));  // open: out0, out11, out12, out13, out14, out15
  RAM #(.addrWidth(10), .clearpin("true"), .dataWidth(60)) ram_1 (
    .addr(multiplexer_1_out), .we(ram_load_read_controller_1_store), .oe(ram_load_read_controller_1_load),
    .clk(clock_1_out), .din(in_2), .dout(ram_1_dout), .clr(and_2_out));
  RAM #(.addrWidth(10), .clearpin("true"), .dataWidth(40)) ram_2 (
    .addr(multiplexer_2_out), .we(ram_load_read_controller_1_store), .oe(ram_load_read_controller_1_load),
    .clk(clock_1_out), .din(in_4), .dout(ram_2_dout), .clr(and_2_out));
  RAM #(.addrWidth(10), .clearpin("true"), .dataWidth(60)) ram_3 (
    .addr(multiplexer_5_out), .we(ram_load_read_controller_2_store), .oe(ram_load_read_controller_2_load),
    .clk(clock_1_out), .din(in_2), .dout(ram_3_dout), .clr(and_2_out));
  Multiplexer #(.width(10)) multiplexer_5 (.in0(PC_q), .in1(RELOAD), .out(multiplexer_5_out), .sel(not_3_out));
  RAM #(.addrWidth(10), .clearpin("true"), .dataWidth(40)) ram_4 (
    .addr(multiplexer_3_out), .we(ram_load_read_controller_2_store), .oe(ram_load_read_controller_2_load),
    .clk(clock_1_out), .din(in_4), .dout(ram_4_dout), .clr(and_2_out));
  assign bit_extender_7_out = {{4{1'b0}}, multiplexer_4_out};  // Bit_Extender bit_extender_7
  assign bit_extender_8_out = {{28{1'b0}}, multiplexer_6_out};  // Bit_Extender bit_extender_8
  Multiplexer #(.select(3), .width(24)) multiplexer_6 (
    .in0(adder_1_out), .in1(subtractor_1_out), .in2(and_1_out), .in3(or_1_out), .in4(xor_1_out),
    .in5(not_2_out), .in6(bit_extender_5_out), .in7(bit_extender_6_out), .out(multiplexer_6_out),
    .sel(SIMPLE_ALU_DATA_q[51:49]));
  Counter #(.max('hffffffffff), .width(40)) PC (
    .D({multiplexer_7_out_2[39:14], multiplexer_7_out}), .count(demultiplexer_1_out9), .Q({PC_q_2, PC_q}),
    .up(1'b1), .clk(clock_1_out), .clr(and_2_out));  // open: load, carry
  Register #(.width(52)) R0 (
    .D({multiplexer_7_out_3, multiplexer_7_out_2, multiplexer_7_out}), .en(demultiplexer_1_out3),
    .clk(clock_1_out), .Q(R0_q), .clr(and_2_out));
  Multiplexer #(.select(3), .width(52)) multiplexer_7 (
    .in0(bit_extender_8_out), .in1(bit_extender_7_out), .in2(R0_q), .in3(R1_q), .in4(R2_q), .in5(R3_q),
    .in6(IR_q_3), .in7(CACHE_L2_dout), .out({multiplexer_7_out_3, multiplexer_7_out_2, multiplexer_7_out}),
    .sel(IR_q_2));
  Multiplexer #(.width(60)) multiplexer_8 (
    .in0(ram_1_dout), .in1(ram_3_dout), .out(multiplexer_8_out), .sel(CACHE_IN_READ));
  Multiplexer #(.width(40)) multiplexer_9 (.in0(ram_2_dout), .in1(ram_4_dout), .sel(CACHE_IN_READ));  // open: out
  Register #(.width(52)) R1 (
    .D({multiplexer_7_out_3, multiplexer_7_out_2, multiplexer_7_out}), .en(demultiplexer_1_out4),
    .clk(clock_1_out), .Q(R1_q), .clr(and_2_out));
  Register #(.width(60)) IR (
    .D(multiplexer_8_out), .Q({IR_q_3, IR_q[7], IR_q_2, IR_q[3:0]}), .clk(clock_1_out), .clr(and_2_out));  // open: en
  Register #(.width(52)) R2 (
    .D({multiplexer_7_out_3, multiplexer_7_out_2, multiplexer_7_out}), .en(demultiplexer_1_out5),
    .clk(clock_1_out), .Q(R2_q), .clr(and_2_out));
  Register #(.width(52)) R3 (
    .D({multiplexer_7_out_3, multiplexer_7_out_2, multiplexer_7_out}), .en(demultiplexer_1_out6),
    .clk(clock_1_out), .Q(R3_q), .clr(and_2_out));
  Register #(.width(14)) ADR_CACHE (
    .D(multiplexer_7_out), .en(demultiplexer_1_out10), .Q(ADR_CACHE_q), .clk(clock_1_out), .clr(and_2_out));
  RAM #(.addrWidth(14), .clearpin("true"), .dataWidth(52)) CACHE_L2 (
    .addr(ADR_CACHE_q), .we(ram_load_read_controller_3_store), .oe(ram_load_read_controller_3_load),
    .clk(clock_1_out), .din({multiplexer_7_out_3, multiplexer_7_out_2, multiplexer_7_out}),
    .dout(CACHE_L2_dout), .clr(and_2_out));
  RAM_LOAD_READ_CONTROLLER ram_load_read_controller_3 (
    .STORE_SIGNAL(demultiplexer_1_out7), .LOAD(ram_load_read_controller_3_load),
    .STORE(ram_load_read_controller_3_store));
  Register #(.width(48)) GPU_INST (
    .D({multiplexer_7_out_2, multiplexer_7_out}), .en(demultiplexer_1_out8), .Q(GPU_INST_q),
    .clk(clock_1_out), .clr(and_2_out));
  Counter #(.max('h3f), .width(6)) counter_1 (
    .count(comparator_3_lt), .Q(counter_1_q), .up(1'b1), .clk(clock_1_out), .clr(or_2_out));  // open: load, D, carry
  D_Flip_Flop d_ff_2 (.D(comparator_3_eq), .clk(clock_1_out), .Q(d_ff_2_q), .reset(and_2_out));  // open: Qn, preset
  Adder #(.width(24)) adder_2 (.a(bit_extender_10_out), .b(GPU_INST_q[47:24]), .out(adder_2_out));  // open: cin, cout
  Multiplier #(.width(3)) multiplier_3 (
    .a(GPU_INST_q[20:18]), .b(GPU_INST_q[23:21]), .out(multiplier_3_out), .cout(multiplier_3_cout));  // open: cin
  assign bit_extender_9_out = {{3{1'b0}}, GPU_INST_q[20:18]};  // Bit_Extender bit_extender_9
  or or_2 (or_2_out, and_2_out, demultiplexer_1_out8);
  Counter #(.max('hffff), .width(16)) SCREEN (
    .Q(SCREEN_q), .up(1'b1), .clk(clock_1_out), .clr(and_2_out));  // open: load, D, count, carry
  Adder #(.width(16)) adder_3 (.a(GPU_INST_q[17:2]), .b({out_5, out_6}), .out(adder_3_out));  // open: cin, cout
  not not_4 (not_4_out, d_ff_2_q);
  ROM #(.addrWidth(24), .dataWidth(24)) Resources (.addr(adder_2_out), .data(Resources_data));
  Comparator #(.mode("unsigned"), .width(6)) comparator_3 (
    .a(counter_1_q), .b({multiplier_3_cout, multiplier_3_out}), .eq(comparator_3_eq), .lt(comparator_3_lt));  // open: gt
  Divider #(.width(6)) divider_3 (
    .a(counter_1_q), .b(bit_extender_9_out), .out(divider_3_out), .rem(divider_3_rem));  // open: upper
  assign bit_extender_10_out = {{18{1'b0}}, counter_1_q};  // Bit_Extender bit_extender_10
  and and_3 (and_3_out, comparator_3_eq, not_4_out);
  or or_3 (or_3_out, and_2_out, and_4_out);
  assign out_5 = {{2{1'b0}}, divider_3_out};  // Bit_Extender bit_extender_11
  assign out_6 = {{2{1'b0}}, divider_3_rem};  // Bit_Extender bit_extender_12
  not not_5 (not_5_out, BufferInScreen_q);
  S_R_Flip_Flop s_r_ff_1 (.S(and_3_out), .clk(clock_1_out), .R(or_3_out), .Q(s_r_ff_1_q));  // open: Qn, preset, reset
  Multiplexer #(.width(16)) multiplexer_10 (
    .in0(SCREEN_q), .in1(adder_3_out), .out(multiplexer_10_out), .sel(BufferInScreen_q));
  RAM_LOAD_READ_CONTROLLER ram_load_read_controller_4 (
    .STORE_SIGNAL(BufferInScreen_q), .LOAD(ram_load_read_controller_4_load),
    .STORE(ram_load_read_controller_4_store));
  Multiplexer #(.width(16)) multiplexer_11 (
    .in0(SCREEN_q), .in1(adder_3_out), .out(multiplexer_11_out), .sel(not_5_out));
  Demultiplexer #(.width(24)) demultiplexer_2 (
    .out0(demultiplexer_2_out0), .out1(demultiplexer_2_out1), .in(Resources_data), .sel(not_5_out));
  RAM_LOAD_READ_CONTROLLER ram_load_read_controller_5 (
    .STORE_SIGNAL(not_5_out), .LOAD(ram_load_read_controller_5_load), .STORE(ram_load_read_controller_5_store));
  // RGB_Video #(.cursor("No Cursor"), .height(256), .width(256)) rgb_video_1: pin names not known; wires that end beside it: and_2_out, clock_1_out, 1'b1, SCREEN_q[7:0], SCREEN_q[15:8], rgb_video_1_p6
  Comparator #(.mode("unsigned"), .width(16)) comparator_4 (
    .a(SCREEN_q), .b({16{1'b1}}), .eq(comparator_4_eq));  // open: gt, lt
  RAM #(.addrWidth(16), .clearpin("true"), .dataWidth(24)) FrameBuffer0 (
    .addr(multiplexer_10_out), .we(ram_load_read_controller_4_store), .oe(ram_load_read_controller_4_load),
    .clk(clock_1_out), .din(demultiplexer_2_out0), .dout(FrameBuffer0_dout), .clr(and_2_out));
  RAM #(.addrWidth(16), .clearpin("true"), .dataWidth(24)) FrameBuffer1 (
    .addr(multiplexer_11_out), .we(ram_load_read_controller_5_store), .oe(ram_load_read_controller_5_load),
    .clk(clock_1_out), .din(demultiplexer_2_out1), .dout(FrameBuffer1_dout), .clr(and_2_out));
  and and_4 (and_4_out, comparator_4_eq, s_r_ff_1_q);
  Counter #(.max('h1), .width(1)) BufferInScreen (
    .count(and_4_out), .Q(BufferInScreen_q), .up(1'b1), .clk(clock_1_out), .clr(and_2_out));  // open: load, D, carry
  Multiplexer #(.width(24)) multiplexer_12 (
    .in0(FrameBuffer0_dout), .in1(FrameBuffer1_dout), .out(rgb_video_1_p6), .sel(BufferInScreen_q));

  // Notes on the sheet:
  //   contents of Resources (hex, n*v repeats v):
  //   73*0 5*7cff 0 0 7cff 5*0 7cff 0 7cff 5*0 7cff 0 7cff 5*0 7cff 0 7*7cff 0 7cff 5*0 7cff 0 7cff 5*0
  //   7cff 9*0 6*7cff 0 0 7cff 5*0 7cff 0 7cff 5*0 7cff 0 6*7cff 0 0 7cff 5*0 7cff 0 7cff 5*0 7cff 0
  //   6*7cff 11*0 5*ffffff 0 0 ffffff 5*0 ffffff 0 ffffff 7*0 ffffff 7*0 ffffff 7*0 ffffff 5*0 ffffff 0 0
  //   5*ffffff 10*0 5*ffffff 0 0 0 ffffff 4*0 ffffff 0 0 ffffff 5*0 ffffff 0 ffffff 5*0 ffffff 0 ffffff
  //   5*0 ffffff 0 ffffff 4*0 ffffff 0 0 5*ffffff 11*0 7*ffffff 0 ffffff 7*0 ffffff 7*0 7*ffffff 0 ffffff
  //   7*0 ffffff 7*0 7*ffffff 9*0 7*ffffff 0 ffffff 7*0 ffffff 7*0 7*ffffff 0 ffffff 7*0 ffffff 7*0 ffffff
  //   17*0 4*ffffff 0 0 0 ffffff 4*0 ffffff 0 ffffff 7*0 ffffff 0 0 4*ffffff 0 ffffff 5*0 ffffff 0 0
  //   ffffff 4*0 ffffff 0 0 0 4*ffffff 10*0 ffffff 5*0 ffffff 0 ffffff 5*0 ffffff 0 ffffff 5*0 ffffff 0
  //   7*ffffff 0 ffffff 5*0 ffffff 0 ffffff 5*0 ffffff 0 ffffff 5*0 ffffff 9*0 7*ffffff 4*0 ffffff 7*0
  //   ffffff 7*0 ffffff 7*0 ffffff 7*0 ffffff 4*0 7*ffffff 14*0 ffffff 7*0 ffffff 7*0 ffffff 7*0 ffffff
  //   7*0 ffffff 0 0 0 ffffff 0 0 0 ffffff 4*0 ffffff ffffff ffffff 11*0 ffffff 5*0 ffffff 0 ffffff 5*0
  //   ffffff 0 ffffff 4*0 ffffff 0 0 5*ffffff 0 0 0 ffffff 4*0 ffffff 0 0 ffffff 5*0 ffffff 0 ffffff 5*0
  //   ffffff 10*0 ffffff 7*0 ffffff 7*0 ffffff 7*0 ffffff 7*0 ffffff 7*0 ffffff 7*0 6*ffffff 9*0 ffffff
  //   ffffff 0 0 0 ffffff ffffff 0 ffffff 0 ffffff 0 ffffff 0 ffffff 0 ffffff 0 0 ffffff 0 0 ffffff 0
  //   ffffff 5*0 ffffff 0 ffffff 5*0 ffffff 0 ffffff 5*0 ffffff 0 ffffff 5*0 ffffff 9*0 ffffff 5*0 ffffff
  //   0 ffffff ffffff 4*0 ffffff 0 ffffff 0 ffffff 0 0 0 ffffff 0 ffffff 0 0 ffffff 0 0 ffffff 0 ffffff 0
  //   0 0 ffffff 0 ffffff 0 ffffff 4*0 ffffff ffffff 0 ffffff 5*0 ffffff 9*0 7*ffffff 9*0 ffffff ffffff
  //   4*0 ffffff 0 ffffff 0 ffffff 0 0 0 ffffff 0 ffffff 0 0 ffffff 0 0 ffffff 0 ffffff 0 0 0 ffffff 0
  //   ffffff 0 ffffff 4*0 ffffff ffffff 10*0 5*ffffff 0 0 ffffff 5*0 ffffff 0 ffffff 5*0 ffffff 0 ffffff
  //   5*0 ffffff 0 ffffff 5*0 ffffff 0 ffffff 5*0 ffffff 0 0 5*ffffff 10*0 6*ffffff 0 0 ffffff 5*0 ffffff
  //   0 ffffff 5*0 ffffff 0 ffffff 5*0 ffffff 0 6*ffffff 0 0 ffffff 7*0 ffffff 16*0 5*ffffff 0 0 ffffff
  //   5*0 ffffff 0 ffffff 5*0 ffffff 0 ffffff 5*0 ffffff 0 ffffff 5*0 ffffff 0 ffffff 4*0 ffffff 0 0 0
  //   4*ffffff 0 ffffff 9*0 6*ffffff 0 0 ffffff 5*0 ffffff 0 ffffff 5*0 ffffff 0 ffffff 5*0 ffffff 0
  //   6*ffffff 0 0 ffffff 5*0 ffffff 0 ffffff 5*0 ffffff 10*0 5*ffffff 0 0 ffffff 5*0 ffffff 0 ffffff 8*0
  //   5*ffffff 8*0 ffffff 0 ffffff 5*0 ffffff 0 0 5*ffffff 10*0 7*ffffff 4*0 ffffff 7*0 ffffff 7*0 ffffff
  //   7*0 ffffff 7*0 ffffff 7*0 ffffff 12*0 ffffff 5*0 ffffff 0 ffffff 5*0 ffffff 0 ffffff 5*0 ffffff 0
  //   ffffff 5*0 ffffff 0 ffffff 5*0 ffffff 0 ffffff 5*0 ffffff 0 0 5*ffffff 10*0 ffffff 5*0 ffffff 0
  //   ffffff 5*0 ffffff 0 0 ffffff 0 0 0 ffffff 0 0 0 ffffff 0 0 0 ffffff 4*0 ffffff 0 ffffff 5*0 ffffff 0
  //   ffffff 6*0 ffffff 12*0 ffffff 5*0 ffffff 0 ffffff 5*0 ffffff 0 ffffff 5*0 ffffff 0 ffffff 5*0 ffffff
  //   0 0 ffffff 0 ffffff 0 ffffff 0 0 0 ffffff 0 ffffff 0 ffffff 4*0 ffffff 0 ffffff 11*0 ffffff 5*0
  //   ffffff 0 ffffff 5*0 ffffff 0 0 ffffff 0 0 0 ffffff 4*0 ffffff ffffff ffffff 4*0 ffffff 0 0 0 ffffff
  //   0 0 ffffff 5*0 ffffff 0 ffffff 5*0 ffffff 9*0 ffffff 5*0 ffffff 0 ffffff 5*0 ffffff 0 ffffff 5*0
  //   ffffff 0 0 6*ffffff 7*0 ffffff 0 ffffff 5*0 ffffff 0 0 5*ffffff 10*0 7*ffffff 7*0 ffffff 6*0 ffffff
  //   4*0 ffffff ffffff ffffff 4*0 ffffff 6*0 ffffff 7*0 7*ffffff 26*0 ffffff ffffff ffffff 8*0 ffffff 4*0
  //   4*ffffff 0 0 0 ffffff 0 0 0 ffffff 4*0 ffffff ffffff ffffff 12*0 ffffff 7*0 ffffff 7*0 ffffff 7*0
  //   4*ffffff 4*0 ffffff 0 0 0 ffffff 0 0 0 ffffff 0 0 0 ffffff 0 0 0 4*ffffff 29*0 ffffff ffffff ffffff
  //   4*0 ffffff 0 0 0 ffffff 0 0 0 ffffff 7*0 ffffff 0 0 0 ffffff 4*0 ffffff ffffff ffffff 16*0 ffffff
  //   7*0 ffffff 7*0 ffffff 4*0 4*ffffff 0 0 0 ffffff 0 0 0 ffffff 0 0 0 ffffff 0 0 0 ffffff 4*0 4*ffffff
  //   28*0 ffffff ffffff ffffff 4*0 ffffff 0 0 0 ffffff 0 0 0 5*ffffff 0 0 0 ffffff 8*0 4*ffffff 12*0
  //   ffffff ffffff ffffff 4*0 ffffff 0 0 0 ffffff 0 0 0 ffffff 7*0 ffffff 7*0 4*ffffff 4*0 ffffff 7*0
  //   ffffff 16*0 ffffff ffffff ffffff 4*0 ffffff 0 0 0 ffffff 0 0 0 fff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
endmodule

module RAM_LOAD_READ_CONTROLLER (
  input  STORE_SIGNAL,
  output LOAD,
  output STORE
);

  Demultiplexer demultiplexer_1 (.out0(LOAD), .out1(STORE), .in(1'b1), .sel(STORE_SIGNAL));
endmodule

module DELAY_CIRC (
  input  in_1
);

  wire and_1_out, clock_1_out, not_1_out, register_1_q;

  Register #(.width(1)) register_1 (.D(not_1_out), .en(1'b1), .clk(clock_1_out), .Q(register_1_q), .clr(in_1));
  Clock clock_1 (.out(clock_1_out));
  not not_1 (not_1_out, register_1_q);
  and and_1 (and_1_out, register_1_q, 1'b1);
endmodule
